// Logisim project logic_desk.circ as structural Verilog: 2 circuits, main circuit main
module main (
  input  in_1,
  input  in_2,
  input  in_3,
  input  in_4,
  input  [7:0] in_5,
  input  [7:0] in_6,
  input  in_7,
  input  in_8,
  input  in_9,
  input  in_10,
  input  [1:0] in_11,
  input  [1:0] in_12,
  input  in_13
);

  wire dip74595_1_q1, dip74595_1_q2, dip74595_1_q3, dip74595_1_q4, dip74595_1_q5, dip74595_1_q6,
       dip74595_1_q7, dip74595_1_q8, dip74595_1_q8s, dip74595_2_q1, dip74595_2_q2, dip74595_2_q3,
       dip74595_2_q4, dip74595_2_q5, dip74595_2_q6, dip74595_2_q7, dip74595_2_q8, dip74595_2_q8s,
       n7447_1_pin1, n7447_1_pin2, n7447_1_pin3, n7447_1_pin6, n7447_1_pin7, n7447_1_pin9, n7447_1_pin10,
       n7447_1_pin11, n7447_1_pin12, n7447_1_pin13, n7447_1_pin14, n7447_1_pin15, n7447_2_pin3, n7447_2_pin9,
       n7447_2_pin10, n7447_2_pin11, n7447_2_pin12, n7447_2_pin13, n7447_2_pin14, n7447_2_pin15,
       n7474_1_pin1, n7474_1_pin9, n7474_1_pin13, n7474_2_pin1, n7474_2_pin9, n7474_2_pin13, n74157_1_pin4,
       n74157_1_pin6, n74157_1_pin7, n74157_2_pin4, n74157_2_pin6, n74157_2_pin7, n74164_1_pin3,
       n74164_1_pin4, n74164_1_pin5, n74164_1_pin6, n74164_1_pin10, n74164_1_pin11, n74164_1_pin12,
       n74164_1_pin13, n74164_2_pin3, n74164_2_pin4, n74164_2_pin5, n74164_2_pin6, n74164_2_pin9,
       n74164_2_pin10, n74164_2_pin11, n74164_2_pin12, n74164_2_pin13, n74165_1_pin9, n74165_1_pin10,
       n74165_2_pin9, n74273_1_pin1, n74273_1_pin2, n74273_1_pin5, n74273_1_pin6, n74273_1_pin9,
       n74273_1_pin12, n74273_1_pin15, n74273_1_pin16, n74273_1_pin19, n74273_2_pin1, n74273_2_pin2,
       n74273_2_pin5, n74273_2_pin6, n74273_2_pin9, n74273_2_pin12, n74273_2_pin15, n74273_2_pin16,
       n74273_2_pin19, n74283_1_pin1, n74283_1_pin2, n74283_1_pin4, n74283_1_pin6, n74283_1_pin7,
       n74283_1_pin10, n74283_1_pin11, n74283_1_pin13, n74283_1_pin15, n74283_2_pin1, n74283_2_pin2,
       n74283_2_pin4, n74283_2_pin6, n74283_2_pin7, n74283_2_pin10, n74283_2_pin11, n74283_2_pin13,
       n74283_2_pin15, not_1_out;

  _7447 #(.ShowInternalStructure("true")) u_7447_1 (
    .pin1(n7447_1_pin1), .pin2(n7447_1_pin2), .pin3(n7447_1_pin3), .pin4(n7447_1_pin3), .pin5(n7447_1_pin3),
    .pin6(n7447_1_pin6), .pin7(n7447_1_pin7), .pin15(n7447_1_pin15), .pin14(n7447_1_pin14),
    .pin13(n7447_1_pin13), .pin12(n7447_1_pin12), .pin11(n7447_1_pin11), .pin10(n7447_1_pin10),
    .pin9(n7447_1_pin9));
  Pull_Resistor pull_resistor_1 (.node(in_1));
  not not_1 (not_1_out, in_2);
  _74164 #(.ShowInternalStructure("true")) u_74164_1 (
    .pin1(in_7), .pin2(in_7), .pin3(n74164_1_pin3), .pin4(n74164_1_pin4), .pin5(n74164_1_pin5),
    .pin6(n74164_1_pin6), .pin13(n74164_1_pin13), .pin12(n74164_1_pin12), .pin11(n74164_1_pin11),
    .pin10(n74164_1_pin10), .pin9(not_1_out), .pin8(in_3));
  Pull_Resistor pull_resistor_2 (.node(in_13));
  _74165 #(.ShowInternalStructure("true")) u_74165_1 (
    .pin1(in_10), .pin2(in_9), .pin3(in_5[4]), .pin4(in_5[5]), .pin5(in_5[6]), .pin6(in_5[7]), .pin15(in_8),
    .pin14(in_5[3]), .pin13(in_5[2]), .pin12(in_5[1]), .pin11(in_5[0]), .pin10(n74165_1_pin10),
    .pin9(n74165_1_pin9));  // open: pin7
  _74157 #(.ShowInternalStructure("true")) u_74157_1 (
    .pin1(in_10), .pin2(in_11[0]), .pin3(in_13), .pin4(n74157_1_pin4), .pin5(in_11[1]), .pin6(n74157_1_pin6),
    .pin7(n74157_1_pin7));  // open: pin15, pin14, pin13, pin12, pin11, pin10, pin9
  _7_Segment_Display #(.active("false")) u_7_segment_display_1 (
    .g(n7447_1_pin14), .f(n7447_1_pin15), .a(n7447_1_pin13), .b(n7447_1_pin12), .e(n7447_1_pin9),
    .d(n7447_1_pin10), .c(n7447_1_pin11), .dp(1'b1));
  _74175 u_74175_1 ();  // open: pin1, pin2, pin3, pin4, pin5, pin6, pin7, pin15, pin14, pin13, pin12, pin11, pin10, pin9
  Pull_Resistor pull_resistor_3 (.node(n7447_1_pin6));
  Pull_Resistor pull_resistor_4 (.node(n7447_1_pin7));
  Pull_Resistor pull_resistor_5 (.node(n74165_1_pin10));
  _74273 #(.ShowInternalStructure("true")) u_74273_1 (
    .pin1(n74273_1_pin1), .pin2(n74273_1_pin2), .pin3(n74164_1_pin3), .pin4(n74164_1_pin4),
    .pin5(n74273_1_pin5), .pin6(n74273_1_pin6), .pin7(n74164_1_pin5), .pin8(n74164_1_pin6),
    .pin9(n74273_1_pin9), .pin19(n74273_1_pin19), .pin18(n74164_1_pin13), .pin17(n74164_1_pin12),
    .pin16(n74273_1_pin16), .pin15(n74273_1_pin15), .pin14(n74164_1_pin11), .pin13(n74164_1_pin10),
    .pin12(n74273_1_pin12), .pin11(in_4));
  _7474 #(.ShowInternalStructure("true")) u_7474_1 (
    .pin1(n7474_1_pin1), .pin2(n74157_1_pin4), .pin3(in_9), .pin5(n74157_1_pin6), .pin13(n7474_1_pin13),
    .pin12(n74157_1_pin7), .pin11(in_9), .pin9(n7474_1_pin9));  // open: pin4, pin6, pin10, pin8
  Pull_Resistor pull_resistor_6 (.node(n7447_1_pin2));
  _74283 #(.ShowInternalStructure("true")) u_74283_1 (
    .pin1(n74283_1_pin1), .pin2(n74283_1_pin2), .pin3(n7447_1_pin1), .pin4(n74283_1_pin4),
    .pin5(n7447_1_pin7), .pin6(n74283_1_pin6), .pin7(n74283_1_pin7), .pin15(n74283_1_pin15),
    .pin14(n7447_1_pin2), .pin13(n74283_1_pin13), .pin12(n7447_1_pin6), .pin11(n74283_1_pin11),
    .pin10(n74283_1_pin10));  // open: pin9
  Pull_Resistor pull_resistor_7 (.node(n7447_1_pin1));
  LedBar ledbar_1 (
    .led0(dip74595_1_q1), .led1(dip74595_1_q2), .led2(dip74595_1_q3), .led3(dip74595_1_q4),
    .led4(dip74595_1_q5), .led5(dip74595_1_q6), .led6(dip74595_1_q7), .led7(dip74595_1_q8));
  DIP74595 dip74595_1 (
    .OE(1'b0), .LCLK(in_4), .D(in_1), .SCLK(in_3), .CLR(in_2), .Q1(dip74595_1_q1), .Q2(dip74595_1_q2),
    .Q3(dip74595_1_q3), .Q4(dip74595_1_q4), .Q5(dip74595_1_q5), .Q6(dip74595_1_q6), .Q7(dip74595_1_q7),
    .Q8(dip74595_1_q8), .Q8S(dip74595_1_q8s));
  LedBar ledbar_2 (
    .led0(n74273_1_pin2), .led1(n74273_1_pin5), .led2(n74273_1_pin6), .led3(n74273_1_pin9),
    .led4(n74273_1_pin12), .led5(n74273_1_pin15), .led6(n74273_1_pin16), .led7(n74273_1_pin19));
  Pull_Resistor pull_resistor_8 (.node(dip74595_1_q8s));
  Pull_Resistor pull_resistor_9 (.node(n7474_1_pin9));
  _74165 #(.ShowInternalStructure("true")) u_74165_2 (
    .pin1(in_10), .pin2(in_9), .pin3(in_6[4]), .pin4(in_6[5]), .pin5(in_6[6]), .pin6(in_6[7]), .pin15(in_8),
    .pin14(in_6[3]), .pin13(in_6[2]), .pin12(in_6[1]), .pin11(in_6[0]), .pin10(n74165_1_pin9),
    .pin9(n74165_2_pin9));  // open: pin7
  _74157 #(.ShowInternalStructure("true")) u_74157_2 (
    .pin1(in_10), .pin2(in_12[0]), .pin3(n7474_1_pin9), .pin4(n74157_2_pin4), .pin5(in_12[1]),
    .pin6(n74157_2_pin6), .pin7(n74157_2_pin7));  // open: pin15, pin14, pin13, pin12, pin11, pin10, pin9
  _7447 #(.ShowInternalStructure("true")) u_7447_2 (
    .pin1(n74283_1_pin1), .pin2(n74283_1_pin13), .pin3(n7447_2_pin3), .pin4(n7447_2_pin3),
    .pin5(n7447_2_pin3), .pin6(n74283_1_pin10), .pin7(n74283_1_pin4), .pin15(n7447_2_pin15),
    .pin14(n7447_2_pin14), .pin13(n7447_2_pin13), .pin12(n7447_2_pin12), .pin11(n7447_2_pin11),
    .pin10(n7447_2_pin10), .pin9(n7447_2_pin9));
  Pull_Resistor pull_resistor_10 (.node(n74165_1_pin9));
  _74164 #(.ShowInternalStructure("true")) u_74164_2 (
    .pin1(n74164_1_pin4), .pin2(n74164_1_pin4), .pin3(n74164_2_pin3), .pin4(n74164_2_pin4),
    .pin5(n74164_2_pin5), .pin6(n74164_2_pin6), .pin13(n74164_2_pin13), .pin12(n74164_2_pin12),
    .pin11(n74164_2_pin11), .pin10(n74164_2_pin10), .pin9(n74164_2_pin9), .pin8(in_3));
  LED led_1 (.in(n74165_2_pin9));
  not not_2 (n74164_2_pin9, in_2);
  _7474 #(.ShowInternalStructure("true")) u_7474_2 (
    .pin1(n7474_2_pin1), .pin2(n74157_2_pin4), .pin3(in_9), .pin5(n74157_2_pin6), .pin13(n7474_2_pin13),
    .pin12(n74157_2_pin7), .pin11(in_9), .pin9(n7474_2_pin9));  // open: pin4, pin6, pin10, pin8
  _7_Segment_Display #(.active("false")) u_7_segment_display_2 (
    .g(n7447_2_pin14), .f(n7447_2_pin15), .a(n7447_2_pin13), .b(n7447_2_pin12), .e(n7447_2_pin9),
    .d(n7447_2_pin10), .c(n7447_2_pin11), .dp(1'b1));
  DIP74595 dip74595_2 (
    .OE(1'b0), .LCLK(in_4), .D(dip74595_1_q8s), .SCLK(in_3), .CLR(in_2), .Q1(dip74595_2_q1),
    .Q2(dip74595_2_q2), .Q3(dip74595_2_q3), .Q4(dip74595_2_q4), .Q5(dip74595_2_q5), .Q6(dip74595_2_q6),
    .Q7(dip74595_2_q7), .Q8(dip74595_2_q8), .Q8S(dip74595_2_q8s));
  _74273 #(.ShowInternalStructure("true")) u_74273_2 (
    .pin1(n74273_2_pin1), .pin2(n74273_2_pin2), .pin3(n74164_2_pin3), .pin4(n74164_2_pin4),
    .pin5(n74273_2_pin5), .pin6(n74273_2_pin6), .pin7(n74164_2_pin5), .pin8(n74164_2_pin6),
    .pin9(n74273_2_pin9), .pin19(n74273_2_pin19), .pin18(n74164_2_pin13), .pin17(n74164_2_pin12),
    .pin16(n74273_2_pin16), .pin15(n74273_2_pin15), .pin14(n74164_2_pin11), .pin13(n74164_2_pin10),
    .pin12(n74273_2_pin12), .pin11(in_4));
  Pull_Resistor pull_resistor_11 (.node(n74283_1_pin10));
  Pull_Resistor pull_resistor_12 (.node(n74283_1_pin4));
  Pull_Resistor pull_resistor_13 (.node(n74283_1_pin1));
  LedBar ledbar_3 (
    .led0(dip74595_2_q1), .led1(dip74595_2_q2), .led2(dip74595_2_q3), .led3(dip74595_2_q4),
    .led4(dip74595_2_q5), .led5(dip74595_2_q6), .led6(dip74595_2_q7), .led7(dip74595_2_q8));
  LedBar ledbar_4 (
    .led0(n74273_2_pin2), .led1(n74273_2_pin5), .led2(n74273_2_pin6), .led3(n74273_2_pin9),
    .led4(n74273_2_pin12), .led5(n74273_2_pin15), .led6(n74273_2_pin16), .led7(n74273_2_pin19));
  LED led_2 (.in(n7474_2_pin9));
  Pull_Resistor pull_resistor_14 (.node(n74283_1_pin13));
  _74283 #(.ShowInternalStructure("true")) u_74283_2 (
    .pin1(n74283_2_pin1), .pin2(n74283_2_pin2), .pin3(n74283_1_pin1), .pin4(n74283_2_pin4),
    .pin5(n74283_1_pin4), .pin6(n74283_2_pin6), .pin7(n74283_2_pin7), .pin15(n74283_2_pin15),
    .pin14(n74283_1_pin13), .pin13(n74283_2_pin13), .pin12(n74283_1_pin10), .pin11(n74283_2_pin11),
    .pin10(n74283_2_pin10));  // open: pin9
  Pull_Resistor pull_resistor_15 (.node(dip74595_2_q8s));
  // also tied to GND on the sheet: {n74283_1_pin15, n74283_1_pin2, n74283_1_pin11, n74283_1_pin6, n74283_2_pin15, n74283_2_pin2, n74283_2_pin11, n74283_2_pin6}
  // also tied to VCC on the sheet: {n7447_1_pin3, n74273_1_pin1, n7474_1_pin1, n7474_1_pin13, n74283_1_pin7, n7447_2_pin3, n7474_2_pin1, n7474_2_pin13, n74273_2_pin1, n74283_2_pin7}

  // Other names for the same wires on the sheet: CLK_IN = in_9; CLK_OUT = in_3; CLR_IN = in_8; CLR_OUT = in_2;
  //   LATCH_IN = in_10; LATCH_OUT = in_4

  // Notes on the sheet:
  //   N-BIT SHIFT OUT
  //   8-BIT SHIFT IN
  //   SELECT LINE ->
  //   8-BIT SHIFT OUT
  //   2-BIT SHIFT IN
endmodule

module DIP74595 (
  input  OE,
  input  LCLK,
  input  D,
  input  SCLK,
  input  CLR,
  output Q1,
  output Q2,
  output Q3,
  output Q4,
  output Q5,
  output Q6,
  output Q7,
  output Q8,
  output Q8S
);

  wire d_ff_1_q, d_ff_2_q, d_ff_3_q, d_ff_4_q, d_ff_5_q, d_ff_6_q, d_ff_7_q, d_ff_9_q, d_ff_10_q, d_ff_11_q,
       d_ff_12_q, d_ff_13_q, d_ff_14_q, d_ff_15_q, d_ff_16_q, not_1_out;

  not not_1 (not_1_out, OE);
  D_Flip_Flop d_ff_1 (.D(D), .clk(SCLK), .Q(d_ff_1_q), .reset(CLR));  // open: Qn, preset
  D_Flip_Flop d_ff_2 (.D(d_ff_1_q), .clk(SCLK), .Q(d_ff_2_q), .reset(CLR));  // open: Qn, preset
  D_Flip_Flop d_ff_3 (.D(d_ff_2_q), .clk(SCLK), .Q(d_ff_3_q), .reset(CLR));  // open: Qn, preset
  D_Flip_Flop d_ff_4 (.D(d_ff_3_q), .clk(SCLK), .Q(d_ff_4_q), .reset(CLR));  // open: Qn, preset
  D_Flip_Flop d_ff_5 (.D(d_ff_4_q), .clk(SCLK), .Q(d_ff_5_q), .reset(CLR));  // open: Qn, preset
  D_Flip_Flop d_ff_6 (.D(d_ff_5_q), .clk(SCLK), .Q(d_ff_6_q), .reset(CLR));  // open: Qn, preset
  D_Flip_Flop d_ff_7 (.D(d_ff_6_q), .clk(SCLK), .Q(d_ff_7_q), .reset(CLR));  // open: Qn, preset
  D_Flip_Flop d_ff_8 (.D(d_ff_7_q), .clk(SCLK), .Q(Q8S), .reset(CLR));  // open: Qn, preset
  D_Flip_Flop d_ff_9 (.D(d_ff_1_q), .clk(LCLK), .Q(d_ff_9_q));  // open: Qn, preset, reset
  D_Flip_Flop d_ff_10 (.D(d_ff_2_q), .clk(LCLK), .Q(d_ff_10_q));  // open: Qn, preset, reset
  D_Flip_Flop d_ff_11 (.D(d_ff_3_q), .clk(LCLK), .Q(d_ff_11_q));  // open: Qn, preset, reset
  D_Flip_Flop d_ff_12 (.D(d_ff_4_q), .clk(LCLK), .Q(d_ff_12_q));  // open: Qn, preset, reset
  D_Flip_Flop d_ff_13 (.D(d_ff_5_q), .clk(LCLK), .Q(d_ff_13_q));  // open: Qn, preset, reset
  D_Flip_Flop d_ff_14 (.D(d_ff_6_q), .clk(LCLK), .Q(d_ff_14_q));  // open: Qn, preset, reset
  D_Flip_Flop d_ff_15 (.D(d_ff_7_q), .clk(LCLK), .Q(d_ff_15_q));  // open: Qn, preset, reset
  D_Flip_Flop d_ff_16 (.D(Q8S), .clk(LCLK), .Q(d_ff_16_q));  // open: Qn, preset, reset
  assign Q1 = not_1_out ? d_ff_9_q : 1'bz;  // Controlled_Buffer controlled_buffer_1
  assign Q2 = not_1_out ? d_ff_10_q : 1'bz;  // Controlled_Buffer controlled_buffer_2
  assign Q3 = not_1_out ? d_ff_11_q : 1'bz;  // Controlled_Buffer controlled_buffer_3
  assign Q4 = not_1_out ? d_ff_12_q : 1'bz;  // Controlled_Buffer controlled_buffer_4
  assign Q5 = not_1_out ? d_ff_13_q : 1'bz;  // Controlled_Buffer controlled_buffer_5
  assign Q6 = not_1_out ? d_ff_14_q : 1'bz;  // Controlled_Buffer controlled_buffer_6
  assign Q7 = not_1_out ? d_ff_15_q : 1'bz;  // Controlled_Buffer controlled_buffer_7
  assign Q8 = not_1_out ? d_ff_16_q : 1'bz;  // Controlled_Buffer controlled_buffer_8
endmodule
